// Logisim project LogicGate_AND_ThreeInputs.circ as structural Verilog: 1 circuit, main circuit main
module main (
  input  in_1,
  input  in_2,
  input  in_3
);

  wire and_1_out;

  and and_1 (and_1_out, in_1, in_2, in_3);
  LED led_1 (.in(and_1_out));
endmodule
