// Logisim project LogicGate_NOR_ORNOT.circ as structural Verilog: 1 circuit, main circuit main
module main (
  input  in_1,
  input  in_2
);

  wire not_1_out, or_1_out;

  or or_1 (or_1_out, in_1, in_2);
  not not_1 (not_1_out, or_1_out);
  LED led_1 (.in(not_1_out));
endmodule
